// Logisim project Multiplexers.circ as structural Verilog: 1 circuit, main circuit main
module main (
  input  in_1,
  input  in_2,
  input  in_3,
  input  in_4,
  input  in_5,
  input  [1:0] in_6,
  input  so,
  input  s1_bar,
  input  enable,
  input  \do ,
  input  d1,
  input  d2,
  input  d3
);

  wire and_1_out, and_2_out, and_3_out, and_4_out, multiplexer_1_out, not_1_out, not_2_out, or_1_out,
       undriven;

  Multiplexer #(.select(2)) multiplexer_1 (
    .in0(in_1), .in1(in_2), .in2(in_3), .in3(in_4), .out(multiplexer_1_out), .sel(in_6), .en(undriven));
  not not_1 (not_1_out, so);
  LED led_1 (.in(multiplexer_1_out));
  not not_2 (not_2_out, s1_bar);
  and and_1 (and_1_out, enable, \do , not_2_out, not_1_out);
  and and_2 (and_2_out, enable, d1, not_2_out, so);
  and and_3 (and_3_out, enable, d2, s1_bar, not_1_out);
  and and_4 (and_4_out, enable, d3, s1_bar, so);
  or or_1 (or_1_out, and_1_out, and_2_out, and_3_out, and_4_out);
  LED led_2 (.in(or_1_out));

  // Notes on the sheet:
  //   s0 bar
  //   s1
  //   y
endmodule
