// Logisim project Demultiplexers.circ as structural Verilog: 1 circuit, main circuit main
module main (
  input  in_1,
  input  in_2,
  input  [1:0] in_3,
  input  s0_bar,
  input  in_5,
  input  s1,
  input  Din
);

  wire and_1_out, and_2_out, and_3_out, and_4_out, demultiplexer_1_out0, demultiplexer_1_out1,
       demultiplexer_1_out2, demultiplexer_1_out3, not_1_out, not_2_out;

  Demultiplexer #(.select(2)) demultiplexer_1 (
    .out0(demultiplexer_1_out0), .out1(demultiplexer_1_out1), .out2(demultiplexer_1_out2),
    .out3(demultiplexer_1_out3), .in(in_1), .sel(in_3), .en(in_2));
  LED led_1 (.in(demultiplexer_1_out3));
  not not_1 (not_1_out, s0_bar);
  LED led_2 (.in(demultiplexer_1_out0));
  LED led_3 (.in(demultiplexer_1_out1));
  LED led_4 (.in(demultiplexer_1_out2));
  not not_2 (not_2_out, s1);
  and and_1 (and_1_out, not_2_out, Din, in_5, not_1_out);
  and and_2 (and_2_out, not_2_out, Din, in_5, s0_bar);
  and and_3 (and_3_out, s1, Din, in_5, not_1_out);
  and and_4 (and_4_out, s1, Din, in_5, s0_bar);
  LED led_5 (.in(and_1_out));
  LED led_6 (.in(and_2_out));
  LED led_7 (.in(and_3_out));
  LED led_8 (.in(and_4_out));

  // Notes on the sheet:
  //   s1 bar
endmodule
