// Logisim project adder_subtractors.circ as structural Verilog: 1 circuit, main circuit main
module main (
  input  A,
  input  A_2,
  input  B,
  input  B_2,
  input  A_3,
  input  B_3,
  input  Cin,
  input  A_4,
  input  B_4,
  input  Bin
);

  wire AND_2_out, AND_3_out, AND_4_out, AND_5_out, AND_6_out, AND_7_out, AND_8_out, AND_out, not_1_out,
       not_2_out, not_3_out, OR_2_out, OR_out, XOR_2_out, XOR_3_out, XOR_4_out, XOR_5_out, XOR_6_out, XOR_out;

  xor XOR (XOR_out, A, B);
  and AND (AND_out, A, B);
  xor XOR_2 (XOR_2_out, A_3, B_3);
  and AND_2 (AND_2_out, A_3, B_3);
  and AND_3 (AND_3_out, Cin, B_3);
  and AND_4 (AND_4_out, A_3, Cin);
  xor XOR_3 (XOR_3_out, A_4, B_4);
  LED led_1 (.in(XOR_out));
  LED led_2 (.in(AND_out));
  xor XOR_4 (XOR_4_out, XOR_2_out, Cin);
  or OR (OR_out, AND_2_out, AND_3_out, AND_4_out);
  xor XOR_5 (XOR_5_out, XOR_3_out, Bin);
  not not_1 (not_1_out, A_4);
  not not_2 (not_2_out, A_4);
  LED CARRY (.in(OR_out));
  and AND_5 (AND_5_out, B_4, Bin);
  and AND_6 (AND_6_out, not_1_out, B_4);
  and AND_7 (AND_7_out, not_2_out, Bin);
  LED SUM (.in(XOR_4_out));
  LED DIFF (.in(XOR_5_out));
  not not_3 (not_3_out, A_2);
  LED BORROW (.in(OR_2_out));
  or OR_2 (OR_2_out, AND_5_out, AND_6_out, AND_7_out);
  xor XOR_6 (XOR_6_out, A_2, B_2);
  and AND_8 (AND_8_out, not_3_out, B_2);
  LED DIFF_2 (.in(XOR_6_out));
  LED BORROW_2 (.in(AND_8_out));

  // Notes on the sheet:
  //   Full Adder
  //   Full Subtracter
  //   Half Adder 
  //   SUM
  //   CARRY
  //   Half Subtracter
endmodule
