// Logisim project basicgates.circ as structural Verilog: 1 circuit, main circuit main
module main (
  input  in_1,
  input  in_2,
  input  A,
  input  in_4,
  input  B,
  input  in_6,
  input  in_7,
  input  in_8,
  input  in_9,
  input  in_10,
  input  in_11,
  input  in_12,
  input  in_13
);

  wire and_1_out, nand_1_out, nor_1_out, not_1_out, or_1_out, xnor_1_out, xor_1_out;

  not not_1 (not_1_out, in_1);
  LED led_1 (.in(not_1_out));
  and and_1 (and_1_out, A, B);
  or or_1 (or_1_out, in_6, in_8);
  nand nand_1 (nand_1_out, in_10, in_11);
  nor nor_1 (nor_1_out, in_12, in_13);
  LED led_2 (.in(and_1_out));
  LED led_3 (.in(or_1_out));
  LED led_4 (.in(nand_1_out));
  LED led_5 (.in(nor_1_out));
  xor xor_1 (xor_1_out, in_2, in_4);
  xnor xnor_1 (xnor_1_out, in_7, in_9);
  LED led_6 (.in(xor_1_out));
  LED led_7 (.in(xnor_1_out));

  // Notes on the sheet:
  //   NOT
  //   AND
  //   OR
  //   NAND
  //   NOR
  //   XOR
  //   XNOR
endmodule
